// Logisim project branch-comp.circ as structural Verilog: 1 circuit, main circuit branch_comp
module branch_comp (
  input  [31:0] BrData1,
  input  [31:0] BrData2,
  input  BrUn,
  output BrEq,
  output BrLt
);

  wire comparator_1_eq, comparator_2_eq, comparator_3_lt, comparator_4_lt;

  Comparator #(.width(32)) comparator_1 (.a(BrData1), .b(BrData2), .eq(comparator_1_eq));  // open: gt, lt
  Comparator #(.mode("unsigned"), .width(32)) comparator_2 (
    .a(BrData1), .b(BrData2), .eq(comparator_2_eq));  // open: gt, lt
  Comparator #(.width(32)) comparator_3 (.a(BrData1), .b(BrData2), .lt(comparator_3_lt));  // open: gt, eq
  Comparator #(.mode("unsigned"), .width(32)) comparator_4 (
    .a(BrData1), .b(BrData2), .lt(comparator_4_lt));  // open: gt, eq
  Multiplexer multiplexer_1 (.in0(comparator_1_eq), .in1(comparator_2_eq), .out(BrEq), .sel(BrUn));
  Multiplexer multiplexer_2 (.in0(comparator_3_lt), .in1(comparator_4_lt), .out(BrLt), .sel(BrUn));

  // Notes on the sheet:
  //   INPUTS to your circuit
  //   是否相等
  //   是否小于
  //   DON'T CHANGE THE LOCATIONS OF THE INPUTS AND OUTPUTS!
  //   signed
  //   Unsigned
  //   signed
  //   Unsigned
  //   OUTPUT from your circuit
endmodule
