// Logisim project control-logic.circ as structural Verilog: 1 circuit, main circuit control_logic
module control_logic (
  input  [31:0] Instruction,
  input  BrEq,
  input  BrLt,
  output PCSel,
  output RegWEn,
  output [2:0] ImmSel,
  output BrUn,
  output ASel,
  output BSel,
  output [3:0] ALUSel,
  output MemWEn,
  output [1:0] WBSel
);

  wire and_1_out, and_2_out, and_3_out, and_4_out, and_5_out, and_6_out, andSel, bSel_t, comparator_1_eq,
       comparator_2_eq, comparator_3_eq, comparator_4_eq, comparator_5_eq, comparator_6_eq, comparator_7_eq,
       comparator_8_eq, comparator_9_eq, comparator_10_eq, comparator_11_eq, comparator_12_eq,
       comparator_13_eq, comparator_14_eq, comparator_15_eq, comparator_16_eq, comparator_17_eq,
       comparator_18_eq, comparator_19_eq, comparator_20_eq, comparator_21_eq, comparator_22_eq,
       comparator_23_eq, comparator_24_eq, comparator_25_eq, comparator_26_eq, comparator_27_eq,
       comparator_28_eq, comparator_29_eq, comparator_30_eq, comparator_31_eq, comparator_32_eq,
       comparator_33_eq, comparator_34_eq, comparator_35_eq, comparator_36_eq, comparator_37_eq,
       comparator_38_eq, comparator_39_eq, comparator_40_eq, comparator_41_eq, comparator_42_eq,
       comparator_43_eq, comparator_44_eq, comparator_45_eq, comparator_46_eq, comparator_47_eq,
       comparator_48_eq, comparator_49_eq, comparator_50_eq, comparator_51_eq, comparator_52_eq,
       comparator_53_eq, comparator_54_eq, comparator_55_eq, comparator_56_eq, comparator_57_eq,
       comparator_58_eq, comparator_59_eq, comparator_60_eq, comparator_61_eq, comparator_63_eq,
       comparator_64_eq, comparator_65_eq, comparator_66_eq, comparator_67_eq, comparator_68_eq,
       comparator_69_eq, comparator_70_eq, comparator_71_eq, comparator_72_eq, comparator_73_eq,
       comparator_74_eq, comparator_75_eq, comparator_76_eq, comparator_77_eq, mulhSel, mulhuSel, mulSel,
       not_1_out, not_2_out, not_3_out, or_1_out, or_2_out, or_3_out, or_5_out, or_6_out, or_10_out,
       or_11_out, or_12_out, or_13_out, or_14_out, or_15_out, or_16_out, or_17_out, or_18_out, or_19_out,
       orSel, sllSel, sltSel, sraSel, srlSel, subSel, xorSel;
  wire [1:0] multiplexer_12_out;
  wire [2:0] multiplexer_1_out, multiplexer_2_out, multiplexer_3_out;
  wire [3:0] multiplexer_5_out, multiplexer_6_out, multiplexer_7_out, multiplexer_8_out, multiplexer_9_out,
       multiplexer_10_out, multiplexer_11_out, multiplexer_13_out, multiplexer_15_out, multiplexer_16_out,
       multiplexer_17_out;
  wire [15:0] rom_1_data;

  Comparator #(.width(7)) comparator_1 (.a(Instruction[6:0]), .b(7'b1100011), .eq(comparator_1_eq));  // open: gt, lt
  Comparator #(.width(7)) comparator_2 (.a(Instruction[6:0]), .b(7'b1100111), .eq(comparator_2_eq));  // open: gt, lt
  Comparator #(.width(7)) comparator_3 (.a(Instruction[6:0]), .b(7'b1101111), .eq(comparator_3_eq));  // open: gt, lt
  Comparator #(.width(7)) comparator_4 (.a(Instruction[6:0]), .b(7'b1101111), .eq(comparator_4_eq));  // open: gt, lt
  Comparator #(.width(7)) comparator_5 (.a(Instruction[6:0]), .b(7'b0110111), .eq(comparator_5_eq));  // open: gt, lt
  Comparator #(.width(7)) comparator_6 (.a(Instruction[6:0]), .b(7'b0010111), .eq(comparator_6_eq));  // open: gt, lt
  Comparator #(.width(7)) comparator_7 (.a(Instruction[6:0]), .b(7'b1100111), .eq(comparator_7_eq));  // open: gt, lt
  Comparator #(.width(7)) comparator_8 (.a(Instruction[6:0]), .b(7'b0110011), .eq(comparator_8_eq));  // open: gt, lt
  Comparator #(.width(7)) comparator_9 (.a(Instruction[6:0]), .b(7'b0010011), .eq(comparator_9_eq));  // open: gt, lt
  Comparator #(.width(7)) comparator_10 (.a(Instruction[6:0]), .b(7'b0000011), .eq(comparator_10_eq));  // open: gt, lt
  Comparator #(.width(7)) comparator_11 (.a(Instruction[6:0]), .b(7'b0100011), .eq(comparator_11_eq));  // open: gt, lt
  Comparator #(.width(3)) comparator_12 (.a(Instruction[14:12]), .b(3'b000), .eq(comparator_12_eq));  // open: gt, lt
  Comparator #(.width(3)) comparator_13 (.a(Instruction[14:12]), .b(3'b001), .eq(comparator_13_eq));  // open: gt, lt
  Comparator #(.width(3)) comparator_14 (.a(Instruction[14:12]), .b(3'b100), .eq(comparator_14_eq));  // open: gt, lt
  Comparator #(.width(3)) comparator_15 (.a(Instruction[14:12]), .b(3'b110), .eq(comparator_15_eq));  // open: gt, lt
  Comparator #(.width(3)) comparator_16 (.a(Instruction[14:12]), .b(3'b101), .eq(comparator_16_eq));  // open: gt, lt
  Comparator #(.width(3)) comparator_17 (.a(Instruction[14:12]), .b(3'b111), .eq(comparator_17_eq));  // open: gt, lt
  Multiplexer #(.width(3)) multiplexer_1 (.in0(3'b000), .in1(3'b001), .out(multiplexer_1_out), .sel(comparator_11_eq));
  Comparator #(.width(7)) comparator_18 (.a(Instruction[6:0]), .b(7'b0010111), .eq(comparator_18_eq));  // open: gt, lt
  Comparator #(.width(7)) comparator_19 (.a(Instruction[6:0]), .b(7'b0110111), .eq(comparator_19_eq));  // open: gt, lt
  not not_1 (not_1_out, BrEq);
  not not_2 (not_2_out, BrLt);
  not not_3 (not_3_out, BrLt);
  Multiplexer #(.width(3)) multiplexer_2 (
    .in0(multiplexer_1_out), .in1(3'b010), .out(multiplexer_2_out), .sel(comparator_20_eq));
  Comparator #(.width(7)) comparator_20 (.a(Instruction[6:0]), .b(7'b1100011), .eq(comparator_20_eq));  // open: gt, lt
  and and_1 (and_1_out, comparator_1_eq, comparator_12_eq, BrEq);
  and and_2 (and_2_out, comparator_1_eq, comparator_13_eq, not_1_out);
  and and_3 (and_3_out, comparator_1_eq, comparator_14_eq, BrLt);
  and and_4 (and_4_out, comparator_1_eq, comparator_15_eq, BrLt);
  and and_5 (and_5_out, comparator_1_eq, comparator_16_eq, not_2_out);
  and and_6 (and_6_out, comparator_1_eq, comparator_17_eq, not_3_out);
  or or_1 (or_1_out, comparator_4_eq, comparator_5_eq, comparator_6_eq);
  or or_2 (or_2_out, comparator_8_eq, comparator_9_eq, comparator_10_eq);
  or or_3 (or_3_out, comparator_18_eq, comparator_19_eq);
  Comparator #(.width(7)) comparator_21 (.a(Instruction[6:0]), .b(7'b1101111), .eq(comparator_21_eq));  // open: gt, lt
  or or_4 (RegWEn, or_1_out, comparator_7_eq, or_2_out);
  Multiplexer #(.width(3)) multiplexer_3 (
    .in0(multiplexer_2_out), .in1(3'b011), .out(multiplexer_3_out), .sel(or_3_out));
  or or_5 (or_5_out, and_1_out, and_2_out, and_3_out, and_4_out, and_5_out, and_6_out);
  or or_6 (or_6_out, comparator_2_eq, comparator_3_eq);
  Multiplexer #(.width(3)) multiplexer_4 (.in0(multiplexer_3_out), .in1(3'b100), .out(ImmSel), .sel(comparator_21_eq));
  or or_7 (PCSel, or_5_out, or_6_out);
  Multiplexer #(.width(4)) multiplexer_5 (.in0(4'b0000), .in1(4'b0001), .out(multiplexer_5_out), .sel(sllSel));
  Comparator #(.width(7)) comparator_22 (.a(Instruction[6:0]), .b(7'b1100011), .eq(comparator_22_eq));  // open: gt, lt
  Comparator #(.width(7)) comparator_23 (.a(Instruction[6:0]), .b(7'b0010111), .eq(comparator_23_eq));  // open: gt, lt
  Comparator #(.width(7)) comparator_24 (.a(Instruction[6:0]), .b(7'b1101111), .eq(comparator_24_eq));  // open: gt, lt
  Comparator #(.width(7)) comparator_25 (.a(Instruction[6:0]), .b(7'b0010011), .eq(comparator_25_eq));  // open: gt, lt
  Comparator #(.width(7)) comparator_26 (.a(Instruction[6:0]), .b(7'b0100011), .eq(comparator_26_eq));  // open: gt, lt
  Comparator #(.width(7)) comparator_27 (.a(Instruction[6:0]), .b(7'b0000011), .eq(comparator_27_eq));  // open: gt, lt
  Comparator #(.width(7)) comparator_28 (.a(Instruction[6:0]), .b(7'b1100011), .eq(comparator_28_eq));  // open: gt, lt
  Comparator #(.width(7)) comparator_29 (.a(Instruction[6:0]), .b(7'b1100111), .eq(comparator_29_eq));  // open: gt, lt
  Comparator #(.width(7)) comparator_30 (.a(Instruction[6:0]), .b(7'b0010111), .eq(comparator_30_eq));  // open: gt, lt
  Comparator #(.width(7)) comparator_31 (.a(Instruction[6:0]), .b(7'b0110111), .eq(comparator_31_eq));  // open: gt, lt
  Comparator #(.width(7)) comparator_32 (.a(Instruction[6:0]), .b(7'b1101111), .eq(comparator_32_eq));  // open: gt, lt
  Multiplexer #(.width(4)) multiplexer_6 (
    .in0(multiplexer_5_out), .in1(4'b0010), .out(multiplexer_6_out), .sel(sltSel));
  or or_8 (ASel, comparator_22_eq, comparator_23_eq, comparator_24_eq);
  or or_9 (BSel, comparator_25_eq, comparator_26_eq, comparator_27_eq, comparator_28_eq, comparator_29_eq, comparator_30_eq, comparator_31_eq, comparator_32_eq);
  Multiplexer #(.width(4)) multiplexer_7 (
    .in0(multiplexer_6_out), .in1(4'b1011), .out(multiplexer_7_out), .sel(mulhuSel));
  Comparator #(.width(7)) comparator_33 (.a(Instruction[31:25]), .b({7{1'b0}}), .eq(comparator_33_eq));  // open: gt, lt
  Comparator #(.width(3)) comparator_34 (.a(Instruction[14:12]), .b(3'b001), .eq(comparator_34_eq));  // open: gt, lt
  Comparator #(.width(7)) comparator_35 (.a(Instruction[6:0]), .b(7'b0110011), .eq(comparator_35_eq));  // open: gt, lt
  Comparator #(.width(7)) comparator_36 (.a(Instruction[6:0]), .b(7'b0010011), .eq(comparator_36_eq));  // open: gt, lt
  Comparator #(.width(3)) comparator_37 (.a(Instruction[14:12]), .b(3'b011), .eq(comparator_37_eq));  // open: gt, lt
  Comparator #(.width(7)) comparator_38 (.a(Instruction[6:0]), .b(7'b0110011), .eq(comparator_38_eq));  // open: gt, lt
  Comparator #(.width(3)) comparator_39 (.a(Instruction[14:12]), .b(3'b100), .eq(comparator_39_eq));  // open: gt, lt
  Comparator #(.width(7)) comparator_40 (.a(Instruction[6:0]), .b(7'b0110011), .eq(comparator_40_eq));  // open: gt, lt
  Comparator #(.width(7)) comparator_41 (.a(Instruction[6:0]), .b(7'b0010011), .eq(comparator_41_eq));  // open: gt, lt
  Comparator #(.width(7)) comparator_42 (.a(Instruction[31:25]), .b({7{1'b0}}), .eq(comparator_42_eq));  // open: gt, lt
  Comparator #(.width(3)) comparator_43 (.a(Instruction[14:12]), .b(3'b101), .eq(comparator_43_eq));  // open: gt, lt
  Comparator #(.width(7)) comparator_44 (.a(Instruction[6:0]), .b(7'b0110011), .eq(comparator_44_eq));  // open: gt, lt
  Comparator #(.width(7)) comparator_45 (.a(Instruction[6:0]), .b(7'b0010011), .eq(comparator_45_eq));  // open: gt, lt
  Comparator #(.width(3)) comparator_46 (.a(Instruction[14:12]), .b(3'b110), .eq(comparator_46_eq));  // open: gt, lt
  Comparator #(.width(7)) comparator_47 (.a(Instruction[6:0]), .b(7'b0110011), .eq(comparator_47_eq));  // open: gt, lt
  Comparator #(.width(7)) comparator_48 (.a(Instruction[6:0]), .b(7'b0010011), .eq(comparator_48_eq));  // open: gt, lt
  Comparator #(.width(3)) comparator_49 (.a(Instruction[14:12]), .b(3'b111), .eq(comparator_49_eq));  // open: gt, lt
  Comparator #(.width(7)) comparator_50 (.a(Instruction[6:0]), .b(7'b0110011), .eq(comparator_50_eq));  // open: gt, lt
  Comparator #(.width(7)) comparator_51 (.a(Instruction[6:0]), .b(7'b0010011), .eq(comparator_51_eq));  // open: gt, lt
  or or_10 (or_10_out, comparator_35_eq, comparator_36_eq);
  Comparator #(.width(3)) comparator_52 (.a(Instruction[14:12]), .b(3'b010), .eq(comparator_52_eq));  // open: gt, lt
  Comparator #(.width(7)) comparator_53 (.a(Instruction[6:0]), .b(7'b0110011), .eq(comparator_53_eq));  // open: gt, lt
  Comparator #(.width(7)) comparator_54 (.a(Instruction[6:0]), .b(7'b0010011), .eq(comparator_54_eq));  // open: gt, lt
  or or_11 (or_11_out, comparator_44_eq, comparator_45_eq);
  Multiplexer #(.width(4)) multiplexer_8 (
    .in0(multiplexer_7_out), .in1(4'b0100), .out(multiplexer_8_out), .sel(xorSel));
  or or_12 (or_12_out, comparator_53_eq, comparator_54_eq);
  or or_13 (or_13_out, comparator_40_eq, comparator_41_eq);
  or or_14 (or_14_out, comparator_47_eq, comparator_48_eq);
  or or_15 (or_15_out, comparator_50_eq, comparator_51_eq);
  and and_7 (sllSel, comparator_33_eq, comparator_34_eq, or_10_out);
  and and_8 (sltSel, comparator_52_eq, or_12_out);
  and and_9 (mulhuSel, comparator_37_eq, comparator_38_eq);
  and and_10 (xorSel, comparator_39_eq, or_13_out);
  and and_11 (srlSel, comparator_42_eq, comparator_43_eq, or_11_out);
  and and_12 (orSel, comparator_46_eq, or_14_out);
  and and_13 (andSel, comparator_49_eq, or_15_out);
  Multiplexer #(.width(4)) multiplexer_9 (
    .in0(multiplexer_8_out), .in1(4'b0101), .out(multiplexer_9_out), .sel(srlSel));
  Comparator #(.width(7)) comparator_55 (.a(Instruction[6:0]), .b(7'b0110011), .eq(comparator_55_eq));  // open: gt, lt
  Comparator #(.width(7)) comparator_56 (.a(Instruction[6:0]), .b(7'b0010011), .eq(comparator_56_eq));  // open: gt, lt
  Comparator #(.width(7)) comparator_57 (.a(Instruction[6:0]), .b(7'b0010111), .eq(comparator_57_eq));  // open: gt, lt
  Comparator #(.width(7)) comparator_58 (.a(Instruction[6:0]), .b(7'b0110111), .eq(comparator_58_eq));  // open: gt, lt
  Comparator #(.width(7)) comparator_59 (.a(Instruction[6:0]), .b(7'b1100011), .eq(comparator_59_eq));  // open: gt, lt
  Comparator #(.width(3)) comparator_60 (.a(Instruction[14:12]), .b(3'b110), .eq(comparator_60_eq));  // open: gt, lt
  Comparator #(.width(3)) comparator_61 (.a(Instruction[14:12]), .b(3'b111), .eq(comparator_61_eq));  // open: gt, lt
  Comparator #(.width(7)) comparator_62 (.a(Instruction[6:0]), .b(7'b0100011), .eq(MemWEn));  // open: gt, lt
  Multiplexer #(.width(4)) multiplexer_10 (
    .in0(multiplexer_9_out), .in1(4'b0110), .out(multiplexer_10_out), .sel(orSel));
  or or_16 (or_16_out, comparator_60_eq, comparator_61_eq);
  and and_14 (BrUn, comparator_59_eq, or_16_out);
  or or_17 (or_17_out, comparator_55_eq, comparator_56_eq, comparator_57_eq, comparator_58_eq);
  Comparator #(.width(7)) comparator_63 (.a(Instruction[6:0]), .b(7'b1100111), .eq(comparator_63_eq));  // open: gt, lt
  Comparator #(.width(7)) comparator_64 (.a(Instruction[6:0]), .b(7'b1101111), .eq(comparator_64_eq));  // open: gt, lt
  Multiplexer #(.width(4)) multiplexer_11 (
    .in0(multiplexer_10_out), .in1(4'b0111), .out(multiplexer_11_out), .sel(andSel));
  Multiplexer #(.width(2)) multiplexer_12 (.in0(2'b00), .in1(2'b01), .out(multiplexer_12_out), .sel(or_17_out));
  Comparator #(.width(7)) comparator_65 (
    .a(Instruction[31:25]), .b(7'b0100000), .eq(comparator_65_eq));  // open: gt, lt
  Comparator #(.width(3)) comparator_66 (.a(Instruction[14:12]), .b(3'b000), .eq(comparator_66_eq));  // open: gt, lt
  Comparator #(.width(7)) comparator_67 (.a(Instruction[6:0]), .b(7'b0110011), .eq(comparator_67_eq));  // open: gt, lt
  Comparator #(.width(7)) comparator_68 (
    .a(Instruction[31:25]), .b(7'b0000001), .eq(comparator_68_eq));  // open: gt, lt
  Comparator #(.width(3)) comparator_69 (.a(Instruction[14:12]), .b(3'b001), .eq(comparator_69_eq));  // open: gt, lt
  Comparator #(.width(7)) comparator_70 (.a(Instruction[6:0]), .b(7'b0110011), .eq(comparator_70_eq));  // open: gt, lt
  Comparator #(.width(7)) comparator_71 (
    .a(Instruction[31:25]), .b(7'b0100000), .eq(comparator_71_eq));  // open: gt, lt
  Comparator #(.width(3)) comparator_72 (.a(Instruction[14:12]), .b(3'b101), .eq(comparator_72_eq));  // open: gt, lt
  Comparator #(.width(7)) comparator_73 (.a(Instruction[6:0]), .b(7'b0110011), .eq(comparator_73_eq));  // open: gt, lt
  Comparator #(.width(7)) comparator_74 (.a(Instruction[6:0]), .b(7'b0010011), .eq(comparator_74_eq));  // open: gt, lt
  or or_18 (or_18_out, comparator_63_eq, comparator_64_eq);
  Multiplexer #(.width(4)) multiplexer_13 (
    .in0(multiplexer_11_out), .in1(4'b1100), .out(multiplexer_13_out), .sel(subSel));
  Comparator #(.width(7)) comparator_75 (
    .a(Instruction[31:25]), .b(7'b0000001), .eq(comparator_75_eq));  // open: gt, lt
  Comparator #(.width(3)) comparator_76 (.a(Instruction[14:12]), .b(3'b000), .eq(comparator_76_eq));  // open: gt, lt
  Comparator #(.width(7)) comparator_77 (.a(Instruction[6:0]), .b(7'b0110011), .eq(comparator_77_eq));  // open: gt, lt
  Comparator #(.width(7)) comparator_78 (.a(Instruction[6:0]), .b(7'b0110111), .eq(bSel_t));  // open: gt, lt
  Multiplexer #(.width(2)) multiplexer_14 (.in0(multiplexer_12_out), .in1(2'b10), .out(WBSel), .sel(or_18_out));
  Multiplexer #(.width(4)) multiplexer_15 (
    .in0(multiplexer_13_out), .in1(4'b1001), .out(multiplexer_15_out), .sel(mulhSel));
  or or_19 (or_19_out, comparator_73_eq, comparator_74_eq);
  and and_15 (subSel, comparator_65_eq, comparator_66_eq, comparator_67_eq);
  and and_16 (mulhSel, comparator_68_eq, comparator_69_eq, comparator_70_eq);
  and and_17 (sraSel, comparator_71_eq, comparator_72_eq, or_19_out);
  Multiplexer #(.width(4)) multiplexer_16 (
    .in0(multiplexer_15_out), .in1(4'b1101), .out(multiplexer_16_out), .sel(sraSel));
  and and_18 (mulSel, comparator_75_eq, comparator_76_eq, comparator_77_eq);
  ROM #(.addrWidth(6), .dataWidth(16)) rom_1 (.data(rom_1_data));  // open: addr
  Multiplexer #(.width(4)) multiplexer_17 (
    .in0(multiplexer_16_out), .in1(4'b1000), .out(multiplexer_17_out), .sel(mulSel));
  Multiplexer #(.width(4)) multiplexer_18 (.in0(multiplexer_17_out), .in1(4'b1111), .out(ALUSel), .sel(bSel_t));

  // Other names for the same wires on the sheet: opcode[6:0] = Instruction[6:0]; rd[4:0] = Instruction[11:7];
  //   func3[2:0] = Instruction[14:12]; rs1[4:0] = Instruction[19:15]; rs2[4:0] = Instruction[24:20];
  //   func7[6:0] = Instruction[31:25]

  // Notes on the sheet:
  //   INPUTS to your circuit
  //   B-type
  //   I-type中的jalr
  //   J-type中的jal
  //   S-type
  //   jalr
  //   jal
  //   B-type
  //   U-type
  //   I-type
  //   jal
  //   lui
  //   auipc
  //   jalr
  //   R
  //   I
  //   load
  //   J-type
  //   PC选择控制
  //   Reg是否可写控制
  //   立即数类型选择控制
  //   DON'T CHANGE THE LOCATIONS OF THE INPUTS AND OUTPUTS!
  //   auipc
  //   lui
  //   OUTPUT from your circuit
  //   beq
  //   bnq
  //   blt
  //   bltu
  //   bge
  //   bgeu
  //   I-type
  //   S-type
  //   I-type中的jarl
  //   U-type中的auipc
  //   U-type中的lui
  //   I-type中的jar
  //   B-type
  //   U-type中的auipc
  //   J-type中的jal
  //   I-type中的load
  //   B-type
  //   add
  //   Docode
  //   func7 rs2 rs1 func3 rd opcode
  //   Asel:选DataA还是PC
  //   Bsel: 选DataB还是imm
  //   需要不同运算的指令类型
  //   fun3(0x)
  //   运算类型
  //   对应的ALUSel
  //   R-instr
  //   I-instr
  //   R-instr
  //   R-instr
  //   I-instr
  //   R-instr
  //   I-instr
  //   R-instr
  //   I-instr
  //   R-instr
  //   I-instr
  //   0
  //   add
  //   sub
  //   mul
  //   0
  //   12
  //   8
  //   R-instr
  //   I-instr
  //   fun7(0x)
  //   00
  //   20
  //   01
  //   R或I类型
  //   类型
  //   R/I
  //   R
  //   R
  //   1
  //   sll
  //   mulh
  //   1
  //   9
  //   fun7(0x)
  //   00
  //   01
  //   R
  //   I
  //   auipc
  //   lui
  //   类型
  //   R/I
  //   R
  //   2
  //   slt
  //   2
  //   是否符号启用符号比较
  //   B-type
  //   S-type
  //   类型
  //   R/I
  //   jalr
  //   jal
  //   其余类型只需要用加法运算
  //   3
  //   mulhu
  //   11
  //   R-instr
  //   R-instr
  //   R-instr
  //   I-instr
  //   如果为S类型指令，内存设置为写入1
  //   写回控制
  //   类型
  //   R
  //   R-instr
  //   load
  //   ALU
  //   4
  //   xor
  //   4
  //   类型
  //   R/I
  //   PC+4
  //   5
  //   srl
  //   sra
  //   5
  //   13
  //   U类型的lui直接将立即数(imm)加载到目标寄存器（rd）
  //   U-instr
  //   fun7(0x)
  //   00
  //   20
  //   类型
  //   R/I
  //   R/I
  //   6
  //   or
  //   6
  //   Connect ROM Input here ->
  //   7
  //   类型
  //   R/I
  //   and
  //   类型
  //   R/I
  //   7
  //   ROM FOR CONTROL LOGIC
  //   This is only if you choose to do the ROM option
  //   CONNECT
  //   WIRE
  //   TO
  //   USE
  //   ROM
  //   Reminder: If using ROM, use combinational logic for PCSel
endmodule
