// Logisim project cpu.circ as structural Verilog: 1 circuit, main circuit cpu
module cpu (
  input  clk,
  input  [31:0] Instruction,
  input  [31:0] MemReadData,
  output [31:0] MemAddress,
  output [31:0] ProgramCounter,
  output [31:0] ra,
  output [31:0] sp,
  output [31:0] t0,
  output [31:0] t1,
  output [31:0] t2,
  output [31:0] s0,
  output [31:0] s1,
  output [31:0] a0,
  output [3:0] MemWriteMask,
  output [31:0] MemWriteData
);

  wire branch_comp_1_breq, branch_comp_1_brlt, control_logic_1_asel, control_logic_1_brun,
       control_logic_1_bsel, control_logic_1_memwen, control_logic_1_pcsel, control_logic_1_regwen;
  wire [1:0] control_logic_1_wbsel;
  wire [2:0] control_logic_1_immsel;
  wire [3:0] control_logic_1_alusel;
  wire [4:0] register_4_q_2, register_4_q_3, register_4_q_4;
  wire [31:0] adder_1_out, imm_gen_1_immediate, multiplexer_1_out, multiplexer_2_out, multiplexer_3_out,
       multiplexer_4_out, multiplexer_5_out, partial_load_1_datatoreg, regfile_1_readdata1,
       regfile_1_readdata2, register_2_q, register_3_q, register_4_q;

  Multiplexer #(.width(32)) multiplexer_1 (
    .in0(adder_1_out), .in1(MemAddress), .out(multiplexer_1_out), .sel(control_logic_1_pcsel));
  Register #(.width(32)) register_1 (.D(multiplexer_1_out), .clk(clk), .Q(ProgramCounter));  // open: en, clr
  Adder #(.width(32)) adder_1 (.a(32'h4), .b(ProgramCounter), .out(adder_1_out));  // open: cin, cout
  Multiplexer #(.width(32)) multiplexer_2 (
    .in0(Instruction), .in1(32'h13), .out(multiplexer_2_out), .sel(control_logic_1_pcsel));
  Register #(.width(32)) register_2 (.D(adder_1_out), .clk(clk), .Q(register_2_q));  // open: en, clr
  Register #(.width(32)) register_3 (.D(ProgramCounter), .clk(clk), .Q(register_3_q));  // open: en, clr
  Register #(.width(32)) register_4 (
    .D(multiplexer_2_out), .clk(clk),
    .Q({register_4_q[31:25], register_4_q_4, register_4_q_3, register_4_q[14:12], register_4_q_2, register_4_q[6:0]}));  // open: en, clr
  control_logic control_logic_1 (
    .Instruction({register_4_q[31:25], register_4_q_4, register_4_q_3, register_4_q[14:12], register_4_q_2, register_4_q[6:0]}),
    .BrEq(branch_comp_1_breq), .BrLt(branch_comp_1_brlt), .PCSel(control_logic_1_pcsel),
    .RegWEn(control_logic_1_regwen), .ImmSel(control_logic_1_immsel), .BrUn(control_logic_1_brun),
    .ASel(control_logic_1_asel), .BSel(control_logic_1_bsel), .ALUSel(control_logic_1_alusel),
    .MemWEn(control_logic_1_memwen), .WBSel(control_logic_1_wbsel));
  imm_gen imm_gen_1 (
    .Instruction({register_4_q[31:25], register_4_q_4, register_4_q_3, register_4_q[14:12], register_4_q_2, register_4_q[6:0]}),
    .ImmSel(control_logic_1_immsel), .Immediate(imm_gen_1_immediate));
  regfile regfile_1 (
    .ReadIndex1(register_4_q_3), .ReadIndex2(register_4_q_4), .WriteIndex(register_4_q_2),
    .WriteData(multiplexer_5_out), .RegWEn(control_logic_1_regwen), .clk(clk), .ra(ra), .sp(sp), .t0(t0),
    .t1(t1), .t2(t2), .s0(s0), .s1(s1), .a0(a0), .ReadData1(regfile_1_readdata1),
    .ReadData2(regfile_1_readdata2));
  branch_comp branch_comp_1 (
    .BrData1(regfile_1_readdata1), .BrData2(regfile_1_readdata2), .BrUn(control_logic_1_brun),
    .BrEq(branch_comp_1_breq), .BrLt(branch_comp_1_brlt));
  Multiplexer #(.width(32)) multiplexer_3 (
    .in0(regfile_1_readdata1), .in1(register_3_q), .out(multiplexer_3_out), .sel(control_logic_1_asel));
  Multiplexer #(.width(32)) multiplexer_4 (
    .in0(regfile_1_readdata2), .in1(imm_gen_1_immediate), .out(multiplexer_4_out), .sel(control_logic_1_bsel));
  alu alu_1 (.A(multiplexer_3_out), .B(multiplexer_4_out), .ALUSel(control_logic_1_alusel), .ALUResult(MemAddress));
  partial_store partial_store_1 (
    .Instruction({register_4_q[31:25], register_4_q_4, register_4_q_3, register_4_q[14:12], register_4_q_2, register_4_q[6:0]}),
    .MemAddress(MemAddress), .DataFromReg(regfile_1_readdata2), .MemWEn(control_logic_1_memwen),
    .MemWriteMask(MemWriteMask), .DataToMem(MemWriteData));
  partial_load partial_load_1 (
    .Instruction({register_4_q[31:25], register_4_q_4, register_4_q_3, register_4_q[14:12], register_4_q_2, register_4_q[6:0]}),
    .MemAddress(MemAddress), .DataFromMem(MemReadData), .DataToReg(partial_load_1_datatoreg));
  Multiplexer #(.select(2), .width(32)) multiplexer_5 (
    .in0(partial_load_1_datatoreg), .in1(MemAddress), .in2(register_2_q), .out(multiplexer_5_out),
    .sel(control_logic_1_wbsel));  // open: in3

  // Notes on the sheet:
  //   To IMEM
  //   IMEM (do **NOT** move this)
  //   From IMEM
  //   IF取指阶段
  //   nop
  //   |
  //   |
  //   |
  //   |
  //   |
  //   <--------
  //   |
  //   |
  //   |
  //   |
  //   <--------
  //   |
  //   |
  //   |
  //   |
  //   <--------
  //   |
  //   |
  //   加了这三个寄存器，保证两个取指阶段的PC和Istruction同步
  //   |
  //   |
  //   |
  //   |
  //   |
  //   |
  //   |
  //   |
  //   |
  //   |
  //   |
  //   |
  //   |
  //   |
  //   |
  //   |
  //   |
  //   |
  //   |
  //   |
  //   |
  //   |
  //   |
  //   |
  //   |
  //   |
  //   |
  //   |
  //   |
  //   |
  //   |
  //   |
  //   |
  //   |
  //   |
  //   Inputs/Outputs for testing. Do **NOT** move these.
  //   It is OK to move the PC, RegFile, ALU, MEM, Branch Comp, Imm Gen, Partial Load, Partial Store and Control Logic to wherever is most convenient for you when constructing your CPU, and to delete this text
  //   AddrA
  //   AddrB
  //   AddrD
  //   DataD
  //   EX执行阶段
  //   To DMEM
  //   DMEM (do **NOT** move this)
  //   From DMEM
  //   1
  //   PC
  //   0
  //   4
  //   8
  //   12
  //   16
  //   20
  //   24
  //   在IMEM中pc对应的指令如下
  //   Instruction
  //   加法指令
  //   减法指令
  //   跳转/分支指令
  //   乘法指令
  //   加法指令
  //   加法指令
  //   减法指令
  //   |
  //   |
  //   |
  //   |
  //   |
  //   |
  //   |
  //   |
  //   |
  //   |
  //   |
  //   |
  //   |
  //   |
  //   |
  //   |
  //   |
  //   |
  //   |
  //   |
  //   |
  //   |
  //   |
  //   |
  //   |
  //   |
  //   |
  //   |
  //   流水线思路
  //   PC
  //   0
  //   4
  //   8
  //   12
  //   20
  //   24
  //   Instruction
  //   减法指令
  //   跳转/分支指令
  //   乘法指令
  //   加法指令
  //   减法指令
  //   加法指令
  //   流水线cpu中pc对应的指令如下
  //   PC2
  //   0
  //   4
  //   8
  //   12
  //   20
  //   Instruction2
  //   加法指令
  //   减法指令
  //   跳转/分支指令
  //   nop
  //   加法指令
  //   <------假如跳转到PC=20
  //   <------当涉及到跳转指令时，Instruction此刻不应该加载乘法指令，因此应该用nop指令替代（对应16进制0x13）
endmodule
